# Fritzing sketch protothreads_arduino (saved by Fritzing 0.9.3b)
circuit board: 7.0417cm x 5.50703cm
breadboards: 1

parts:
  Componente1 = Arduino Uno (Rev3)
  S1 = Pushbutton [package="[SMD]"]
  S2 = Pushbutton [package="[SMD]"]
  S3 = Pushbutton [package="[SMD]"]
  LED1 = smd LED [color="Red (633nm)" package="1206 [SMD]"]
  LED2 = smd LED [color="Red (633nm)" package="1206 [SMD]"]
  LED3 = smd LED [color="Red (633nm)" package="1206 [SMD]"]

nets:
  N1: Componente1.D10_PWM/SS, LED1.cathode
  N2: Componente1.D11_PWM/MOSI, LED2.cathode
  N3: Componente1.D12/MISO, LED3.cathode
  GND: Componente1.GND, S1.Pin_1, S1.Pin_2, S2.Pin_1, S2.Pin_2, S3.Pin_1, S3.Pin_2, LED1.anode, LED2.anode, LED3.anode
  N4: Componente1.D2, S2.Pin_3, S2.Pin_4
  N5: Componente1.D3_PWM, S1.Pin_3, S1.Pin_4
  N6: Componente1.D4, S3.Pin_3, S3.Pin_4
  5V: Componente1.5V
